// Logisim project SRM.circ as structural Verilog: 5 circuits, main circuit main
module main (
  input  BO,
  output [15:0] Bus_Output,
  output [11:0] out_3,
  output [11:0] Address,
  output [15:0] out_5,
  output [15:0] Sum,
  output [15:0] out_7,
  output [3:0] Opcode
);

  wire AI, and_1_out, AO, AR, BI, C, CE, Clock_out, CO, EO, HLT, II, IO, J, MI, OI, RI, RO, SU, Z;
  wire [0:0] rom_1_data;
  wire [2:0] counter_1_q;
  wire [3:0] ram_1_data_2;
  wire [8:7] register_2_q;
  wire [11:0] Instruction_Register_value, MAR_output, ram_1_data;
  wire [15:0] bit_extender_1_out, Instruction_Register_output, Out_value;

  Register #(.width(1)) register_1 (.D(C), .en(1'b1), .Q(register_2_q[8]), .clk(and_1_out), .clr(AR));
  Button Reset (.out(AR));
  Counter #(.width(3), .max('h5), .trigger("falling")) counter_1 (
    .count(1'b1), .Q(counter_1_q), .clk(and_1_out), .clr(AR));  // open: load, D, carry
  Register #(.width(1)) register_2 (.D(Z), .en(1'b1), .Q(register_2_q[7]), .clk(and_1_out), .clr(AR));
  register_12 MAR (
    .Output(MAR_output), .Data(ram_1_data), .Value(Address), .Clock(and_1_out), .Load(1'b1), .Reset(AR),
    .Enable(MI));
  register_16 Instruction_Register (
    .Output(Instruction_Register_output), .Data({ram_1_data_2, ram_1_data}),
    .Value({Opcode, Instruction_Register_value}), .Clock(and_1_out), .Load(IO), .Reset(AR), .Enable(II));
  Clock Clock (.out(Clock_out));
  RAM #(.addrWidth(12), .dataWidth(16), .bus("separate")) ram_1 (
    .addr(MAR_output), .din({ram_1_data_2, ram_1_data}), .data({ram_1_data_2, ram_1_data}), .str(RI),
    .clk(and_1_out), .ld(RO));  // open: sel, clr
  ROM #(.addrWidth(9), .dataWidth(16)) rom_1 (
    .addr({register_2_q, Opcode, counter_1_q}),
    .data({HLT, MI, RI, RO, IO, II, AI, AO, EO, SU, BI, OI, CE, CO, J, rom_1_data[0]}));  // open: sel
  assign Bus_Output = 1'b1 ? {ram_1_data_2, ram_1_data} : 16'bz;  // Controlled_Buffer controlled_buffer_1
  and and_1 (and_1_out, Clock_out, ~HLT);  // AND_Gate
  assign bit_extender_1_out = {{4{1'b0}}, Instruction_Register_output[11:0]};  // Bit_Extender bit_extender_1
  assign {ram_1_data_2, ram_1_data} = IO ? bit_extender_1_out : 16'bz;  // Controlled_Buffer controlled_buffer_2
  assign {ram_1_data_2, ram_1_data} = EO ? Sum : 16'bz;  // Controlled_Buffer controlled_buffer_3
  PC pc_1 (
    .In(ram_1_data), .Output(ram_1_data), .Value(out_3), .Clock(and_1_out), .Jump(J), .Count(CE), .Reset(AR),
    .Out(CO));
  register_16 A (
    .Output({ram_1_data_2, ram_1_data}), .Data({ram_1_data_2, ram_1_data}), .Value(out_5), .Clock(and_1_out),
    .Load(AO), .Reset(AR), .Enable(AI));
  ALU alu_1 (.Sum(Sum), .in1(out_5), .in2(out_7), .SU(SU), .CY(C));
  register_16 B (
    .Output({ram_1_data_2, ram_1_data}), .Data({ram_1_data_2, ram_1_data}), .Value(out_7), .Clock(and_1_out),
    .Load(BO), .Reset(AR), .Enable(BI));
  register_16 Out (
    .Output({ram_1_data_2, ram_1_data}), .Data({ram_1_data_2, ram_1_data}), .Value(Out_value),
    .Clock(and_1_out), .Load(1'b0), .Reset(AR), .Enable(OI));
  Hex_Digit_Display hex_digit_display_1 (.value(Out_value[15:12]));  // open: dp
  Hex_Digit_Display hex_digit_display_2 (.value(Out_value[11:8]));  // open: dp
  Hex_Digit_Display hex_digit_display_3 (.value(Out_value[7:4]));  // open: dp
  Hex_Digit_Display hex_digit_display_4 (.value(Out_value[3:0]));  // open: dp
  nor nor_1 (Z, out_5[0], out_5[1], out_5[2], out_5[3], out_5[4], out_5[5], out_5[6], out_5[7], out_5[8], out_5[9], out_5[10], out_5[11], out_5[12], out_5[13], out_5[14], out_5[15]);

  // Other names for the same wires on the sheet: BR = AR; CR = AR; FR = AR; IR = AR; MCR = AR; MR = AR; OR = AR

  // Notes on the sheet:
  //   RAM
  //   contents of rom_1 (hex, n*v repeats v):
  //   4004 1408 6*0 4004 1408 4800 1200 4*0 4004 1408 4800 1020 280 0 0 0 4004 1408 4800 1020 2c0 0 0 0
  //   4004 1408 4800 2100 4*0 4004 1408 a00 5*0 4004 1408 802 5*0 4004 1408 6*0 4004 1408 6*0 4004 1408
  //   6*0 4004 1408 6*0 4004 1408 6*0 4004 1408 6*0 4004 1408 6*0 4004 1408 110 5*0 4004 1408 8000 5*0
  //   4004 1408 6*0 4004 1408 4800 1200 4*0 4004 1408 4800 1020 280 0 0 0 4004 1408 4800 1020 2c0 0 0 0
  //   4004 1408 4800 2100 4*0 4004 1408 a00 5*0 4004 1408 802 5*0 4004 1408 6*0 4004 1408 802 5*0 4004
  //   1408 6*0 4004 1408 6*0 4004 1408 6*0 4004 1408 6*0 4004 1408 6*0 4004 1408 110 5*0 4004 1408 8000
  //   5*0 4004 1408 6*0 4004 1408 4800 1200 4*0 4004 1408 4800 1020 280 0 0 0 4004 1408 4800 1020 2c0 0 0
  //   0 4004 1408 4800 2100 4*0 4004 1408 a00 5*0 4004 1408 802 5*0 4004 1408 802 5*0 4004 1408 6*0 4004
  //   1408 6*0 4004 1408 6*0 4004 1408 6*0 4004 1408 6*0 4004 1408 6*0 4004 1408 110 5*0 4004 1408 8000
  //   5*0 4004 1408 6*0 4004 1408 4800 1200 4*0 4004 1408 4800 1020 280 0 0 0 4004 1408 4800 1020 2c0 0 0
  //   0 4004 1408 4800 2100 4*0 4004 1408 a00 5*0 4004 1408 802 5*0 4004 1408 802 5*0 4004 1408 802 5*0
  //   4004 1408 6*0 4004 1408 6*0 4004 1408 6*0 4004 1408 6*0 4004 1408 6*0 4004 1408 110 5*0 4004 1408
  //   8000
endmodule

// reg
module register_12 (
  input  [11:0] Data,
  input  Load,
  input  Reset,
  input  Enable,
  input  Clock,
  output [11:0] Value,
  output [11:0] Output
);

  assign Output = Load ? Value : 12'bz;  // Controlled_Buffer controlled_buffer_1
  Register #(.width(12)) register_1 (.D(Data), .en(Enable), .Q(Value), .clk(Clock), .clr(Reset));
endmodule

// reg
module register_16 (
  input  [15:0] Data,
  input  Load,
  input  Reset,
  input  Enable,
  input  Clock,
  output [15:0] Value,
  output [15:0] Output
);

  assign Output = Load ? Value : 16'bz;  // Controlled_Buffer controlled_buffer_1
  Register #(.width(16)) register_1 (.D(Data), .en(Enable), .Q(Value), .clk(Clock), .clr(Reset));
endmodule

module ALU (
  input  [15:0] in1,
  input  SU,
  input  [15:0] in2,
  output CY,
  output [15:0] Sum
);

  wire [15:0] bit_extender_1_out, xor_1_out;

  assign xor_1_out = in2 ^ bit_extender_1_out;  // XOR_Gate xor_1, 16 bits wide
  assign bit_extender_1_out = {{15{SU}}, SU};  // Bit_Extender bit_extender_1
  Adder #(.width(16)) adder_1 (.a(in1), .b(xor_1_out), .out(Sum), .cin(SU), .cout(CY));

  // Notes on the sheet:
  //   SU: pull=down
endmodule

module PC (
  input  Jump,
  input  [11:0] In,
  input  Count,
  input  Reset,
  input  Out,
  input  Clock,
  output [11:0] Value,
  output [11:0] Output
);

  Counter #(.width(12), .max('hfff)) counter_1 (
    .load(Jump), .D(In), .count(Count), .Q(Value), .clk(Clock), .clr(Reset));  // open: carry
  assign Output = Out ? Value : 12'bz;  // Controlled_Buffer controlled_buffer_1
endmodule
